# Fritzing sketch Shop Vac Auto Switch (saved by Fritzing 0.9.3b)

parts:
  ACS712_Current_Sensor1 = ACS712 Current Sensor
  Part1 = Arduino Nano (Rev3.0)
  Power_receptacle_socket1 = AC Power Socket
  IC1 = DIP - 8 pins [chip_label=IC package="DIP (Dual Inline) [THT]"]
  Power_receptacle_socket2 = AC Power Socket
  Part2 = AC Plug

nets:
  VCC: ACS712_Current_Sensor1.VCC, Part1.5V, IC1.pin_3
  N1: ACS712_Current_Sensor1.OUT, Part1.A0
  GND: ACS712_Current_Sensor1.GND, Part1.GND, IC1.pin_2
  N2: Part1.D2, IC1.pin1
  N3: Power_receptacle_socket1.pin_2, Power_receptacle_socket2.pin_2, Part2.pin3
  N4: Power_receptacle_socket1.pin_3, Power_receptacle_socket2.pin_3, Part2.pin2
  N5: IC1.pin_4, Power_receptacle_socket2.pin1
  N6: IC1.pin_5, Part2.pin1

custom parts:
  ACS712 Current Sensor: A breakout board for the Allegro ACS712 is a Hall Effect-based linear current sensor. The module operates at 5V.
  AC Power Socket: Power Entry Connector Receptacle, Female Sockets NEMA 5-15R Panel Mount, Snap-In
  DIP - 8 pins: A DIP stand-in part for whatever IC you want. With 8 pins on a 300mil dual inline package (DIP) footprint.
  AC Plug: AC power plug
